// Logisim project sqrt2.circ as structural Verilog: 14 circuits, main circuit main
module main (
  input  ENABLE,
  input  [15:0] IO_DATA_IN,
  output NAN,
  output PINF,
  output NINF,
  output RESULT,
  output [15:0] IO_DATA_OUT
);

  wire CLK_out;

  Clock CLK (.out(CLK_out));
  sqrt sqrt_1 (
    .CLK(CLK_out), .ENABLE(ENABLE), .IO_DATA_IN(IO_DATA_IN), .IS_NAN(NAN), .IS_PINF(PINF), .IS_NINF(NINF),
    .RESULT(RESULT), .IO_DATA_OUT(IO_DATA_OUT));
endmodule

module sqrt (
  input  CLK,
  input  ENABLE,
  input  [15:0] IO_DATA_IN,
  output IS_NAN,
  output IS_PINF,
  output IS_NINF,
  output RESULT,
  output [15:0] IO_DATA_OUT
);


  assign IO_DATA_OUT = IO_DATA_IN;
  assign IS_NINF = 1'b0;
endmodule

module shift (
  input  [15:0] enter,
  output [15:0] res
);


  assign res = {enter[14:0], 1'b0};
endmodule

module full_substracter (
  input  X,
  input  Y,
  input  B_in,
  output D,
  output B_out
);

  wire and_1_out, and_2_out, not_1_out, not_2_out, xor_1_out;

  xor xor_1 (xor_1_out, X, Y);
  not not_1 (not_1_out, X);
  and and_1 (and_1_out, not_1_out, Y);
  not not_2 (not_2_out, xor_1_out);
  xor xor_2 (D, xor_1_out, B_in);
  and and_2 (and_2_out, B_in, not_2_out);
  or or_1 (B_out, and_2_out, and_1_out);
endmodule

module hulf_substracter (
  input  X,
  input  Y,
  output difference,
  output borrow
);

  wire nand_1_out, nand_2_out, nand_3_out;

  nand nand_1 (nand_1_out, X, Y);
  nand nand_2 (nand_2_out, X, nand_1_out);
  nand nand_3 (nand_3_out, nand_1_out, Y);
  nand nand_4 (difference, nand_2_out, nand_3_out);
  nand nand_5 (borrow, nand_3_out, nand_3_out);
endmodule

module substractor (
  input  [11:0] X,
  input  [11:0] Y,
  output [11:0] result
);

  wire full_substracter_1_b_out, full_substracter_2_b_out, full_substracter_3_b_out,
       full_substracter_4_b_out, full_substracter_5_b_out, full_substracter_6_b_out,
       full_substracter_7_b_out, full_substracter_8_b_out, full_substracter_9_b_out,
       full_substracter_10_b_out, full_substracter_11_b_out;

  full_substracter full_substracter_1 (
    .X(X[0]), .Y(Y[0]), .B_in(1'b0), .D(result[0]), .B_out(full_substracter_1_b_out));
  full_substracter full_substracter_2 (
    .X(X[1]), .Y(Y[1]), .B_in(full_substracter_1_b_out), .D(result[1]), .B_out(full_substracter_2_b_out));
  full_substracter full_substracter_3 (
    .X(X[2]), .Y(Y[2]), .B_in(full_substracter_2_b_out), .D(result[2]), .B_out(full_substracter_3_b_out));
  full_substracter full_substracter_4 (
    .X(X[3]), .Y(Y[3]), .B_in(full_substracter_3_b_out), .D(result[3]), .B_out(full_substracter_4_b_out));
  full_substracter full_substracter_5 (
    .X(X[4]), .Y(Y[4]), .B_in(full_substracter_4_b_out), .D(result[4]), .B_out(full_substracter_5_b_out));
  full_substracter full_substracter_6 (
    .X(X[5]), .Y(Y[5]), .B_in(full_substracter_5_b_out), .D(result[5]), .B_out(full_substracter_6_b_out));
  full_substracter full_substracter_7 (
    .X(X[6]), .Y(Y[6]), .B_in(full_substracter_6_b_out), .D(result[6]), .B_out(full_substracter_7_b_out));
  full_substracter full_substracter_8 (
    .X(X[7]), .Y(Y[7]), .B_in(full_substracter_7_b_out), .D(result[7]), .B_out(full_substracter_8_b_out));
  full_substracter full_substracter_9 (
    .X(X[8]), .Y(Y[8]), .B_in(full_substracter_8_b_out), .D(result[8]), .B_out(full_substracter_9_b_out));
  full_substracter full_substracter_10 (
    .X(X[9]), .Y(Y[9]), .B_in(full_substracter_9_b_out), .D(result[9]), .B_out(full_substracter_10_b_out));
  full_substracter full_substracter_11 (
    .X(X[10]), .Y(Y[10]), .B_in(full_substracter_10_b_out), .D(result[10]), .B_out(full_substracter_11_b_out));
  full_substracter full_substracter_12 (
    .X(X[11]), .Y(Y[11]), .B_in(full_substracter_11_b_out), .D(result[11]));  // open: B_out
endmodule

module Num1_greater_equals_Num2 (
  input  [11:0] Num1,
  input  [11:0] Num2,
  output res
);

  wire comporator_1_equal, comporator_1_greater, comporator_2_equal, comporator_2_greater,
       comporator_3_equal, comporator_3_greater, comporator_4_equal, comporator_4_greater,
       comporator_5_equal, comporator_5_greater, comporator_6_equal, comporator_6_greater,
       comporator_7_equal, comporator_7_greater, comporator_8_equal, comporator_8_greater,
       comporator_9_equal, comporator_9_greater, comporator_10_equal, comporator_10_greater,
       comporator_11_equal, comporator_11_greater, comporator_12_equal, comporator_12_greater;

  comporator comporator_1 (
    .Bit_1(Num1[0]), .Bit_2(Num2[0]), .prev_gt(comporator_2_greater), .prev_eq(comporator_2_equal),
    .greater(comporator_1_greater), .equal(comporator_1_equal));
  comporator comporator_2 (
    .Bit_1(Num1[1]), .Bit_2(Num2[1]), .prev_gt(comporator_3_greater), .prev_eq(comporator_3_equal),
    .greater(comporator_2_greater), .equal(comporator_2_equal));
  comporator comporator_3 (
    .Bit_1(Num1[2]), .Bit_2(Num2[2]), .prev_gt(comporator_4_greater), .prev_eq(comporator_4_equal),
    .greater(comporator_3_greater), .equal(comporator_3_equal));
  comporator comporator_4 (
    .Bit_1(Num1[3]), .Bit_2(Num2[3]), .prev_gt(comporator_5_greater), .prev_eq(comporator_5_equal),
    .greater(comporator_4_greater), .equal(comporator_4_equal));
  comporator comporator_5 (
    .Bit_1(Num1[4]), .Bit_2(Num2[4]), .prev_gt(comporator_6_greater), .prev_eq(comporator_6_equal),
    .greater(comporator_5_greater), .equal(comporator_5_equal));
  comporator comporator_6 (
    .Bit_1(Num1[5]), .Bit_2(Num2[5]), .prev_gt(comporator_7_greater), .prev_eq(comporator_7_equal),
    .greater(comporator_6_greater), .equal(comporator_6_equal));
  comporator comporator_7 (
    .Bit_1(Num1[6]), .Bit_2(Num2[6]), .prev_gt(comporator_8_greater), .prev_eq(comporator_8_equal),
    .greater(comporator_7_greater), .equal(comporator_7_equal));
  comporator comporator_8 (
    .Bit_1(Num1[7]), .Bit_2(Num2[7]), .prev_gt(comporator_9_greater), .prev_eq(comporator_9_equal),
    .greater(comporator_8_greater), .equal(comporator_8_equal));
  comporator comporator_9 (
    .Bit_1(Num1[8]), .Bit_2(Num2[8]), .prev_gt(comporator_10_greater), .prev_eq(comporator_10_equal),
    .greater(comporator_9_greater), .equal(comporator_9_equal));
  comporator comporator_10 (
    .Bit_1(Num1[9]), .Bit_2(Num2[9]), .prev_gt(comporator_11_greater), .prev_eq(comporator_11_equal),
    .greater(comporator_10_greater), .equal(comporator_10_equal));
  comporator comporator_11 (
    .Bit_1(Num1[10]), .Bit_2(Num2[10]), .prev_gt(comporator_12_greater), .prev_eq(comporator_12_equal),
    .greater(comporator_11_greater), .equal(comporator_11_equal));
  comporator comporator_12 (
    .Bit_1(Num1[11]), .Bit_2(Num2[11]), .prev_gt(1'b0), .prev_eq(1'b1), .greater(comporator_12_greater),
    .equal(comporator_12_equal));
  or or_1 (res, comporator_1_greater, comporator_1_equal);
endmodule

module comporator (
  input  Bit_1,
  input  Bit_2,
  input  prev_gt,
  input  prev_eq,
  output greater,
  output equal
);

  wire and_1_out, not_1_out, xnor_1_out;

  not not_1 (not_1_out, Bit_2);
  xnor xnor_1 (xnor_1_out, Bit_1, Bit_2);
  and and_1 (and_1_out, Bit_1, not_1_out, prev_eq);
  or or_1 (greater, and_1_out, prev_gt);
  and and_2 (equal, xnor_1_out, prev_eq);
endmodule

module D_trigger (
  input  C,
  input  D,
  input  enable,
  output Q,
  output not_Q
);

  wire not_1_out;

  not not_1 (not_1_out, D);
  RSC_trigger rsc_trigger_1 (.R(not_1_out), .C(C), .S(D), .enable(enable), .Q(Q), .not_Q(not_Q));
endmodule

module RS_trigger (
  input  R,
  input  S,
  input  enable,
  output Q,
  output not_Q
);

  wire nor_2_out, or_1_out, por_1_out;

  POR por_1 (.out(por_1_out));
  nor nor_1 (Q, R, not_Q);
  nor nor_2 (nor_2_out, Q, S);
  or or_1 (or_1_out, enable, por_1_out);
  or or_2 (not_Q, nor_2_out, or_1_out);
endmodule

module summator (
  input  [11:0] num1,
  input  [11:0] num2,
  output [11:0] res
);

  wire sum_bit_1_carry_out, sum_bit_2_carry_out, sum_bit_3_carry_out, sum_bit_4_carry_out,
       sum_bit_5_carry_out, sum_bit_6_carry_out, sum_bit_7_carry_out, sum_bit_8_carry_out,
       sum_bit_9_carry_out, sum_bit_10_carry_out, sum_bit_11_carry_out;

  sum_bit sum_bit_1 (.carry_in(1'b0), .bit_1(num1[0]), .bit_2(num2[0]), .res(res[0]), .carry_out(sum_bit_1_carry_out));
  sum_bit sum_bit_2 (
    .carry_in(sum_bit_1_carry_out), .bit_1(num1[1]), .bit_2(num2[1]), .res(res[1]),
    .carry_out(sum_bit_2_carry_out));
  sum_bit sum_bit_3 (
    .carry_in(sum_bit_2_carry_out), .bit_1(num1[2]), .bit_2(num2[2]), .res(res[2]),
    .carry_out(sum_bit_3_carry_out));
  sum_bit sum_bit_4 (
    .carry_in(sum_bit_3_carry_out), .bit_1(num1[3]), .bit_2(num2[3]), .res(res[3]),
    .carry_out(sum_bit_4_carry_out));
  sum_bit sum_bit_5 (
    .carry_in(sum_bit_4_carry_out), .bit_1(num1[4]), .bit_2(num2[4]), .res(res[4]),
    .carry_out(sum_bit_5_carry_out));
  sum_bit sum_bit_6 (
    .carry_in(sum_bit_5_carry_out), .bit_1(num1[5]), .bit_2(num2[5]), .res(res[5]),
    .carry_out(sum_bit_6_carry_out));
  sum_bit sum_bit_7 (
    .carry_in(sum_bit_6_carry_out), .bit_1(num1[6]), .bit_2(num2[6]), .res(res[6]),
    .carry_out(sum_bit_7_carry_out));
  sum_bit sum_bit_8 (
    .carry_in(sum_bit_7_carry_out), .bit_1(num1[7]), .bit_2(num1[8]), .res(res[7]),
    .carry_out(sum_bit_8_carry_out));
  sum_bit sum_bit_9 (
    .carry_in(sum_bit_8_carry_out), .bit_1(num1[8]), .bit_2(num2[8]), .res(res[8]),
    .carry_out(sum_bit_9_carry_out));
  sum_bit sum_bit_10 (
    .carry_in(sum_bit_9_carry_out), .bit_1(num1[9]), .bit_2(num2[9]), .res(res[9]),
    .carry_out(sum_bit_10_carry_out));
  sum_bit sum_bit_11 (
    .carry_in(sum_bit_10_carry_out), .bit_1(num1[10]), .bit_2(num2[10]), .res(res[10]),
    .carry_out(sum_bit_11_carry_out));
  sum_bit sum_bit_12 (
    .carry_in(sum_bit_11_carry_out), .bit_1(num1[11]), .bit_2(num2[11]), .res(res[11]));  // open: carry_out

  assign num2[7] = num1[8];
endmodule

module sum_bit (
  input  carry_in,
  input  bit_1,
  input  bit_2,
  output res,
  output carry_out
);

  wire and_1_out, and_2_out, xor_1_out;

  xor xor_1 (xor_1_out, bit_1, bit_2);
  and and_1 (and_1_out, bit_1, bit_2);
  xor xor_2 (res, carry_in, xor_1_out);
  and and_2 (and_2_out, carry_in, xor_1_out);
  or or_1 (carry_out, and_2_out, and_1_out);
endmodule

module RSC_trigger (
  input  R,
  input  C,
  input  S,
  input  enable,
  output Q,
  output not_Q
);

  wire and_1_out, and_2_out;

  and and_1 (and_1_out, R, C);
  and and_2 (and_2_out, C, S);
  RS_trigger rs_trigger_1 (.R(and_1_out), .S(and_2_out), .enable(enable), .Q(Q), .not_Q(not_Q));
endmodule

module memory (
  input  [11:0] number,
  input  r_or_w,
  input  enable,
  output [11:0] out_num
);

  D_trigger d_trigger_1 (.C(r_or_w), .D(number[0]), .enable(enable), .Q(out_num[0]));  // open: not_Q
  D_trigger d_trigger_2 (.C(r_or_w), .D(number[1]), .enable(enable), .Q(out_num[1]));  // open: not_Q
  D_trigger d_trigger_3 (.C(r_or_w), .D(number[2]), .enable(enable), .Q(out_num[2]));  // open: not_Q
  D_trigger d_trigger_4 (.C(r_or_w), .D(number[3]), .enable(enable), .Q(out_num[3]));  // open: not_Q
  D_trigger d_trigger_5 (.C(r_or_w), .D(number[4]), .enable(enable), .Q(out_num[4]));  // open: not_Q
  D_trigger d_trigger_6 (.C(r_or_w), .D(number[5]), .enable(enable), .Q(out_num[5]));  // open: not_Q
  D_trigger d_trigger_7 (.C(r_or_w), .D(number[6]), .enable(enable), .Q(out_num[6]));  // open: not_Q
  D_trigger d_trigger_8 (.C(r_or_w), .D(number[7]), .enable(enable), .Q(out_num[7]));  // open: not_Q
  D_trigger d_trigger_9 (.C(r_or_w), .D(number[8]), .enable(enable), .Q(out_num[8]));  // open: not_Q
  D_trigger d_trigger_10 (.C(r_or_w), .D(number[9]), .enable(enable), .Q(out_num[9]));  // open: not_Q
  D_trigger d_trigger_11 (.C(r_or_w), .D(number[10]), .enable(enable), .Q(out_num[10]));  // open: not_Q
  D_trigger d_trigger_12 (.C(r_or_w), .D(number[11]), .enable(enable), .Q(out_num[11]));  // open: not_Q
endmodule
